# Fritzing sketch wiringLIS3DH (saved by Fritzing 0.9.3b)

parts:
  Part1 = Adafruit RGB Matrix Bonnet for Raspberry Pi [part_number="Adafruit #3211"]
  Part2 = Adafruit LIS3DH [part_number="Adafruit #2809"]

nets:
  N1: Part1.SDA, Part2.SDA
  N2: Part1.SCL, Part2.SCL
  +5V: Part1.+5V, Part2.VIN
  GND: Part1.GND, Part2.GND

custom parts:
  Adafruit RGB Matrix Bonnet for Raspberry Pi: You can now create a dazzling display with your Raspberry Pi with the Adafruit RGB Matrix Bonnet. These boards plug into your Pi and makes it super easy to control RGB matrices such as those we stock in the shop and create a colorful scrolling display or mini LED wall with ease. "Bonnet" boards work on any Raspberry Pi with a 40-pin GPIO header — Zero, Zero W/WH, Model A+, B+, Pi 2 and Pi 3.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
  Adafruit LIS3DH: The LIS3DH is a very popular low power triple-axis accelerometer. It's low-cost, but has just about every 'extra' you'd want in an accelerometer: Three axis sensing, 10-bit precision ±2g/±4g/±8g/±16g selectable scaling Both I2C (2 possible addresses) and SPI interface options Interrupt output Multiple data rate options 1 Hz to 5Khz As low as 2uA current draw (just the chip itself, not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
